# Fritzing sketch esp32dht22v1 (saved by Fritzing 1.0.3b)
breadboards: 1

parts:
  A1 = Arduino Nano ESP32
  RHT3 = Humidity and Temperature Sensor RHT03 [part_number=DHT22]
  R1 = Resistor [tolerance=±5% power=0.25W resistance=220 package=THT]

nets:
  3.3V: A1.Pin_2, RHT3.Vcc, R1.Pin_1
  N1: A1.Pin_4, RHT3.Data-signal, R1.Pin_0
  N2: A1.Pin_14, RHT3.GND_2
  GND: RHT3.GND_1

custom parts:
  Arduino Nano ESP32: Arduino® Nano ESP32 tht.
