# Fritzing sketch esp32-dogm-display (saved by Fritzing 1.0.3b)
breadboards: 1

parts:
  A1 = Arduino Nano ESP32
  M1 = EA dogm162 lcd display [package=THT]  # not connected

nets:
  N1: A1.Pin_14, A1.Pin_19

custom parts:
  Arduino Nano ESP32: Arduino® Nano ESP32 tht.
  EA dogm162 lcd display: EA dogm162 lcd display 16*2.
